// Digital circuit nna1.dig as structural Verilog
module nna1 (
  input  clk
);

  wire and_1_out, and_2_out, and_3_out, and_4_out, and_5_out, not_4_out, switchdt_1_p3, switchdt_2_p3;
  wire [1:0] not_2_out, not_3_out;
  wire [3:0] not_1_out;
  wire [7:0] add_1_s, main_mem_d, PC_q;

  // SwitchDT switchdt_1: pin names not known; wires that end beside it: 1'b1, 1'b0, switchdt_1_p3
  // SwitchDT switchdt_2: pin names not known; wires that end beside it: clk, switchdt_1_p3, switchdt_2_p3
  Add #(.Bits(8)) add_1 (.a(PC_q), .b(8'h2), .c_i(1'b0), .s(add_1_s));  // open: c_o
  Register #(.Bits(8)) PC (.D(add_1_s), .C(switchdt_2_p3), .en(1'b1), .Q(PC_q));
  EEPROM #(.AddrBits(8), .Bits(8)) main_mem (.A(PC_q), .CS(1'b1), .WE(1'b0), .OE(1'b1), .D(main_mem_d));
  assign not_1_out = ~main_mem_d[3:0];  // Not not_1, 4 bits wide
  assign not_2_out = ~main_mem_d[5:4];  // Not not_2, 2 bits wide
  assign not_3_out = ~main_mem_d[7:6];  // Not not_3, 2 bits wide
  and and_1 (and_1_out, not_1_out[3], not_1_out[2], not_1_out[1], not_1_out[0]);
  and and_2 (and_2_out, and_1_out, and_3_out);
  and and_3 (and_3_out, not_3_out[1], not_3_out[0], not_2_out[1], not_2_out[0]);
  LED led_1 (.in(and_2_out));
  and and_4 (and_4_out, not_2_out[0], not_2_out[1], not_3_out[0], not_4_out);
  not not_4 (not_4_out, not_3_out[1]);
  and and_5 (and_5_out, and_1_out, and_4_out);
  LED led_2 (.in(and_5_out));

  // Notes on the sheet:
  //   opcode
  //   arg0
  //   arg1
endmodule
