// Digital circuit bit-eater-v2.dig as structural Verilog
module bit_eater_v2 (
  input  clk
);

  wire add_2_c_o, and_1_out, and_9_out, and_10_out, and_11_out, and_12_out, and_13_out, and_14_out,
       and_19_out, and_20_out, and_22_out, and_23_out, bra, brk, cal, cal_flag, comparator_1_eq,
       comparator_1_lt, d_ff_1_nq, dec, dec_flag, decoder_2_out_0, decoder_2_out_1, decoder_3_out_0,
       decoder_3_out_1, decoder_3_out_2, decoder_3_out_3, decoder_4_out_0, decoder_4_out_1, decoder_4_out_2,
       decoder_4_out_3, decoder_5_out_0, decoder_5_out_1, dread, dwrite, eq, eq_flag, flg, flg_flag, gt,
       gt_flag, inc, inc_flag, jmp, lih, lil, mco, mdb, mov, mpb, mrd, multiplexer_3_out, mwr, nop,
       not_3_out, not_4_out, not_5_out, not_6_out, oflag_out, or_1_out, or_2_out, or_3_out, or_5_out,
       or_6_out, or_7_out, or_8_out, or_9_out, pc_write, reset, reset_on_break_out, sin, sub_2_c_o, xcycle,
       xcycle_next, \xor ;
  wire [1:0] and_7_out;
  wire [3:0] arg, co, curop;
  wire [7:0] add_1_s, add_2_s, addrbus, db, driver_7_out, driver_9_out, mbus, pb, pc, pc_next, r1_q, r2_q,
       r3_q, regin, regout_arg0, regout_arg1, regout_r0, sub_1_s, sub_2_s;

  // Probe on arg[3:2]
  // Probe on arg[1:0]
  Register #(.Bits(8)) u_curop (.D(mbus), .C(clk), .en(~xcycle), .Q({curop, arg}));
  Decoder #(.Selector_Bits(4)) decoder_1 (
    .sel(curop), .out_0(sin), .out_1(eq), .out_2(gt), .out_3(flg), .out_5(bra), .out_6(mco), .out_7(mwr),
    .out_8(mrd), .out_9(lil), .out_10(lih), .out_11(mov), .out_12(cal), .out_13(\xor ), .out_14(inc),
    .out_15(dec));  // open: out_4
  // Probe on curop
  // Probe on arg
  Decoder #(.Selector_Bits(2)) decoder_2 (
    .sel(arg[3:2]), .out_0(decoder_2_out_0), .out_1(decoder_2_out_1));  // open: out_2, out_3
  Decoder #(.Selector_Bits(2)) decoder_3 (
    .sel(arg[1:0]), .out_0(decoder_3_out_0), .out_1(decoder_3_out_1), .out_2(decoder_3_out_2),
    .out_3(decoder_3_out_3));
  and and_1 (and_1_out, sin, decoder_3_out_0);
  or or_1 (or_1_out, lil, lih);
  and and_2 (nop, and_1_out, decoder_2_out_0);
  and and_3 (brk, and_1_out, decoder_2_out_1);
  and and_4 (jmp, decoder_3_out_1, sin);
  and and_5 (mpb, decoder_3_out_2, sin);
  and and_6 (mdb, decoder_3_out_3, sin);
  and and_7 (and_7_out[1], arg[3], ~or_1_out);  // And
  and and_8 (and_7_out[0], arg[2], ~or_1_out);  // And
  Decoder #(.Selector_Bits(2)) decoder_4 (
    .sel(and_7_out), .out_0(decoder_4_out_0), .out_1(decoder_4_out_1), .out_2(decoder_4_out_2),
    .out_3(decoder_4_out_3));
  assign regin = mov ? regout_arg1 : 8'bz;  // Driver driver_1
  and and_9 (and_9_out, decoder_4_out_0, curop[0]);
  and and_10 (and_10_out, decoder_4_out_1, curop[0]);
  and and_11 (and_11_out, decoder_4_out_2, curop[0]);
  and and_12 (and_12_out, decoder_4_out_3, curop[0]);
  assign regin = lil ? {regout_r0[7:4], arg} : 8'bz;  // Driver driver_2
  assign regin = lih ? {arg, regout_r0[3:0]} : 8'bz;  // Driver driver_3
  Comparator #(.Bits(8)) comparator_1 (
    .a(regout_arg0), .b(regout_arg1), .eq(comparator_1_eq), .lt(comparator_1_lt));  // open: gt
  Add #(.Bits(8)) add_1 (.a(regout_arg0), .b({{6{1'b0}}, arg[1:0]}), .c_i(1'b0), .s(add_1_s), .c_o(inc_flag));
  Sub #(.Bits(8)) sub_1 (.a(regout_arg0), .b({{6{1'b0}}, arg[1:0]}), .c_i(1'b0), .s(sub_1_s), .c_o(dec_flag));
  not not_1 (eq_flag, comparator_1_eq);
  not not_2 (gt_flag, comparator_1_lt);
  PullDown #(.Bits(8)) pulldown_1 (.out(regin));
  Register #(.Bits(8)) r0 (.D(regin), .C(clk), .en(and_9_out), .Q(regout_r0));
  Register #(.Bits(8)) r1 (.D(regin), .C(clk), .en(and_10_out), .Q(r1_q));
  Register #(.Bits(8)) r2 (.D(regin), .C(clk), .en(and_11_out), .Q(r2_q));
  Register #(.Bits(8)) r3 (.D(regin), .C(clk), .en(and_12_out), .Q(r3_q));
  Register #(.Bits(8)) u_pb (.D(regout_arg0), .C(clk), .en(mpb), .Q(pb));
  Register #(.Bits(8)) u_db (.D(regout_arg0), .C(clk), .en(mdb), .Q(db));
  Register #(.Bits(4)) u_co (.D(arg), .C(clk), .en(mco), .Q(co));
  assign regin = inc ? add_1_s : 8'bz;  // Driver driver_4
  assign regin = dec ? sub_1_s : 8'bz;  // Driver driver_5
  // Probe on regout_r0
  // Probe on r1_q
  // Probe on r2_q
  // Probe on r3_q
  // Probe on pb
  // Probe on db
  // Probe on co
  or or_2 (or_2_out, reset, mpb);
  not not_3 (not_3_out, oflag_out);
  not not_4 (not_4_out, arg[3]);
  Decoder #(.Selector_Bits(4)) decoder_5 (
    .sel(co), .out_0(decoder_5_out_0), .out_1(decoder_5_out_1));  // open: out_2, out_3, out_4, out_5, out_6, out_7, out_8, out_9, out_10, out_11, out_12, out_13, out_14, out_15
  or or_3 (or_3_out, xcycle, pc_write);
  and and_13 (and_13_out, not_3_out, not_4_out);
  and and_14 (and_14_out, arg[2], arg[3]);
  Multiplexer #(.Selector_Bits(2), .Bits(8)) multiplexer_1 (
    .sel(arg[3:2]), .in_0(regout_r0), .in_1(r1_q), .in_2(r2_q), .in_3(r3_q), .out(regout_arg0));
  Multiplexer #(.Selector_Bits(2), .Bits(8)) multiplexer_2 (
    .sel(arg[1:0]), .in_0(regout_r0), .in_1(r1_q), .in_2(r2_q), .in_3(r3_q), .out(regout_arg1));
  CounterPreset #(.Bits(8), .isProgramCounter("true")) u_PC (
    .en(~xcycle), .C(clk), .dir(1'b0), .in(pc_next), .ld(pc_write), .clr(or_2_out), .out(pc));  // open: ovf
  or or_4 (flg_flag, and_13_out, and_14_out);
  DipSwitch reset_on_break (.out(reset_on_break_out));
  not not_5 (not_5_out, or_3_out);
  or or_5 (or_5_out, mrd, mwr);
  and and_15 (reset, reset_on_break_out, brk);
  assign addrbus = not_5_out ? pc : 8'bz;  // Driver driver_6
  and and_16 (xcycle_next, d_ff_1_nq, or_5_out);
  // Probe on mbus
  // Probe on addrbus
  and and_17 (dwrite, xcycle, mwr);
  and and_18 (dread, xcycle, mrd);
  or or_6 (or_6_out, dwrite, dread);
  assign driver_7_out = or_6_out ? db : 8'bz;  // Driver driver_7
  assign driver_7_out = not_6_out ? pb : 8'bz;  // Driver driver_8
  Add #(.Bits(8)) add_2 (.a(regout_arg0), .b(regout_arg1), .c_i(oflag_out), .s(add_2_s), .c_o(add_2_c_o));
  Sub #(.Bits(8)) sub_2 (.a(regout_arg0), .b(regout_arg1), .c_i(oflag_out), .s(sub_2_s), .c_o(sub_2_c_o));
  not not_6 (not_6_out, or_6_out);
  and and_19 (and_19_out, clk, dwrite);
  D_FF d_ff_1 (.D(xcycle_next), .C(~clk), .Q(xcycle), .nQ(d_ff_1_nq));
  assign driver_9_out = decoder_5_out_0 ? add_2_s : 8'bz;  // Driver driver_9
  assign driver_9_out = decoder_5_out_1 ? sub_2_s : 8'bz;  // Driver driver_10
  or or_7 (or_7_out, mwr, mrd);
  or or_8 (or_8_out, driver_7_out[5], driver_7_out[6], driver_7_out[7]);
  LED led_1 (.in(xcycle));
  Multiplexer #(.Selector_Bits(4)) multiplexer_3 (
    .sel(curop), .in_0(oflag_out), .in_1(eq_flag), .in_2(gt_flag), .in_3(flg_flag), .in_4(oflag_out),
    .in_5(oflag_out), .in_6(oflag_out), .in_7(oflag_out), .in_8(oflag_out), .in_9(oflag_out),
    .in_10(oflag_out), .in_11(oflag_out), .in_12(cal_flag), .in_13(oflag_out), .in_14(inc_flag),
    .in_15(dec_flag), .out(multiplexer_3_out));
  assign regin = cal ? driver_9_out : 8'bz;  // Driver driver_11
  and and_20 (and_20_out, xcycle, or_7_out);
  // Probe on pc
  assign regin = dread ? mbus : 8'bz;  // Driver driver_12
  assign mbus = dwrite ? regout_arg0 : 8'bz;  // Driver driver_13
  EEPROM #(.AddrBits(13), .isProgramMemory("true"), .Bits(8)) eeprom_1 (
    .A({driver_7_out[4:0], addrbus}), .CS(~or_8_out), .WE(and_19_out), .OE(~dwrite), .D(mbus));
  Register oflag (.D(multiplexer_3_out), .C(clk), .en(1'b1), .Q(oflag_out));
  assign addrbus = and_20_out ? regout_arg1 : 8'bz;  // Driver driver_14
  or or_9 (or_9_out, bra, jmp);
  Multiplexer #(.Selector_Bits(4)) multiplexer_4 (
    .sel(co), .in_0(add_2_c_o), .in_1(sub_2_c_o), .in_2(1'b0), .in_3(1'b0), .in_4(1'b0), .in_5(1'b0),
    .in_6(1'b0), .in_7(1'b0), .in_8(1'b0), .in_9(1'b0), .in_10(1'b0), .in_11(1'b0), .in_12(1'b0),
    .in_13(1'b0), .in_14(1'b0), .in_15(1'b0), .out(cal_flag));
  and and_21 (pc_write, or_9_out, ~oflag_out);  // And
  and and_22 (and_22_out, jmp, ~oflag_out);  // And
  assign addrbus = and_22_out ? regout_arg0 : 8'bz;  // Driver driver_15
  and and_23 (and_23_out, bra, ~oflag_out);  // And
  Add #(.Bits(8)) add_3 (.a(addrbus), .b(8'h1), .c_i(1'b0), .s(pc_next));  // open: c_o
  assign addrbus = and_23_out ? {pc[7:4], arg} : 8'bz;  // Driver driver_16

  // Other names for the same wires on the sheet: arg1[1:0] = arg[1:0]; arg0[1:0] = arg[3:2]; reg_we = curop[0];
  //   clock = clk

  // Notes on the sheet:
  //   clk: Hz: 200
  //   op decoder
  //   sin
  //   registers
  //   select r0 on lil,lih ops
  //   lil lih
  //   mov
  //   regin_addr
  //   alu
  //   flg
  //   pc,clock
  //   ctrl
  //   val
  //   mwr, mrd
  //   main mem
  //   flag
  //   contents of eeprom_1 (hex, n*v repeats v):
  //   c,10,2f,54,ff,3c,2,65,13,2e,48,a9,12,2e,44,ff,e,7d,3e,15,2e,5c
  //   ,48,17,20,88,8,6f,da,3b,4,b,61,6,6,7,c,12,2e,34,2,44,14,2e,40
  //   ,3,61,6,6,7,c,13,2e,34,20,10,c,1
  //   jmp bra
  //   when bra,jmp put the target value on the addrbus and set pc to target+1
  //   because updates on next cycle
endmodule
